# Fritzing sketch Schaltplan (saved by Fritzing 0.9.3b)

parts:
  W5500_Module1 = W5500 Ethernet module [package="DIP (Dual Inline) [THT]"]
  Bauteil1 = Arduino Uno (Rev3)

nets:
  3.3V: W5500_Module1.3.3V, Bauteil1.3V3
  N1: W5500_Module1.MISO, Bauteil1.D12/MISO
  N2: W5500_Module1.MOSI, Bauteil1.D11_PWM/MOSI
  N3: W5500_Module1.SCS, Bauteil1.D10_PWM/SS
  N4: W5500_Module1.SCLK, Bauteil1.D13/SCK
  GND: W5500_Module1.GND, Bauteil1.GND

custom parts:
  W5500 Ethernet module: W5500 based SPI Ethernet module for Arduino, etc.
