# Fritzing sketch apg25 (saved by Fritzing 0.9.6b)
breadboards: 1

parts:
  Компонент1 = Arduino Uno (Rev3)
  Grove1 = Grove 3 Axis Digital Accelerometer 16g
  T1 = LM34 Temperature Sensor [package="TO92 [THT]"]
  Mod1 = KY-026 Flame Sensor Module [package="Breakout board"]
  S1 = Momentary Switch [package=tactile_switch_smd]
  U1 = 2-Channel 5v Relay Shield [package=relay-2ch5v10a]
  LED1 = LEDs [package=led10mm]
  Компонент2 = IFR520 MOS module [package=THT]
  F1 = Fan - Ventilador [package=THT]
  JACK1 = 2.1mm Barrel Jack with Terminal Block [part_number="Питание 12в 2а"]
  M1 = DC Motor [part_number=Шнек]

nets:
  N1: Компонент1.A0, Mod1.A0
  N2: Компонент1.D8, U1.IN2
  N3: Компонент1.A4/SDA, Grove1.SDA
  N4: Компонент1.A5/SCL, Grove1.SCL
  N5: Компонент1.D3_PWM, T1.Vout
  N6: Компонент1.D4, S1.2
  N7: Компонент1.D5_PWM, Компонент2.SIG
  N8: Компонент1.D7, U1.IN1
  3V3: Компонент1.3V3, Grove1.VCC
  VCC: Компонент1.5V, T1.+Vs, Mod1.VCC, U1.VCC
  GND: Компонент1.GND, Grove1.GND, T1.GND, Mod1.GND, S1.1, U1.GND, Компонент2.GND, JACK1.NEG
  N9: U1.K1-In, LED1.C
  N10: U1.K2-In, M1.pin_2
  N11: Компонент2.V+, F1.5V
  N12: Компонент2.V-, F1.GND
  N13: Компонент2.VIN, JACK1.POS

custom parts:
  KY-026 Flame Sensor Module: KY-026 Flame Sensor Module reacts in the presence of fire.
  2-Channel 5v Relay Shield: 2 Channel 5v Relay Shield w. 2x SPD-06VDC-SD-C
  LEDs: LEDs Standard schematic elements and footprints for 5mm, 3mm, 1206, and 0603 sized LEDs. 5mm - Spark Fun Electronics SKU : COM-00529 (and others)
  Fan - Ventilador: Ventilador de 2 pines, se encuentra comunmente en computadoras de escritorio
